# Fritzing sketch Schema_Capteur_DHT (saved by Fritzing 0.9.3b)
breadboards: 1

parts:
  Composant1 = Arduino Uno (Rev3)
  DHT1 = DHT22 Humidity and Temperature Sensor

nets:
  N1: Composant1.D2, DHT1.DATA
  5V: Composant1.5V, DHT1.VDD
  GND: Composant1.GND, DHT1.GND
