# Fritzing sketch Schema_Thermistance_Capteur (saved by Fritzing 0.9.3b)
breadboards: 1

parts:
  Composant1 = Arduino Uno (Rev3)
  R1 = Resistor [tolerance=±5% resistance=10k package=THT]
  R2 = Temperature Sensor (Thermistor) [thermistor_type=NTC package=THT]
  DHT2 = DHT22 Humidity and Temperature Sensor

nets (from the breadboard view):
  N1: Composant1.A0, R1.Pin_0, R2.pin_0
  N2: Composant1.D2, DHT2.DATA
  5V: Composant1.5V, R1.Pin_1, DHT2.VDD
  GND: Composant1.GND, R2.pin_1, DHT2.GND
